# Fritzing sketch arduino_based_dht_sensor_sketch (saved by Fritzing 0.9.4)
stripboards: 1

parts:
  LED2 = LED - 5mm [color="Green (560nm)" package="5 mm [THT]"]
  LED3 = LED - 5mm [color="Blue (470nm)" package="5 mm [THT]"]
  R1 = Resistor [tolerance=±5% resistance=220 package=THT]
  R2 = Resistor [tolerance=±5% resistance=220 package=THT]
  RHT1 = Humidity and Temperature Sensor RHT03
  J2 = rounded female pin header, 3 pins [form="♀ (female rounded)"]

nets:
  N1: LED2.cathode, LED3.anode, R1.Pin_1, RHT1.Vcc, J2.pin1
  N2: LED2.anode, R2.Pin_1
  N3: R1.Pin_0, R2.Pin_0, RHT1.GND_2, J2.pin2
  N4: RHT1.Data-signal, RHT1.GND_1, J2.pin3
